# Fritzing sketch projeto2_fritzing (saved by Fritzing 0.9.3b)
breadboards: 1

parts:
  Componente1 = Arduino Uno (Rev3)
  LED1 = LED - 5mm [color="Red (633nm)" package="5 mm [THT]"]
  LED2 = LED - 5mm [color="Red (633nm)" package="5 mm [THT]"]
  LED3 = LED - 5mm [color="Red (633nm)" package="5 mm [THT]"]
  R1 = Rotary Potentiometer (Small) [maximum_resistance=100kΩ package=THT]
  S1 = Pushbutton [package="[THT]"]
  S2 = Pushbutton [package="[THT]"]
  LED4 = LED - 5mm [color="Red (633nm)" package="5 mm [THT]"]
  LED5 = LED - 5mm [color="Red (633nm)" package="5 mm [THT]"]
  LED6 = LED - 5mm [color="Red (633nm)" package="5 mm [THT]"]
  M1 = DC Motor
  M2 = DC Motor

nets:
  N1: Componente1.A0, R1.wiper
  N2: Componente1.D8, LED4.cathode
  N3: Componente1.D9_PWM, LED3.cathode
  N4: Componente1.D10_PWM/SS, LED2.cathode
  N5: Componente1.D11_PWM/MOSI, LED1.cathode
  N6: Componente1.D12/MISO, M2.pin_1
  N7: Componente1.D13/SCK, M1.pin_1
  N8: Componente1.GND, LED1.anode, LED2.anode, LED3.anode, R1.leg2, LED4.anode, LED5.anode, LED6.anode
  N9: Componente1.D4, S2.Pin_1, S2.Pin_2
  N10: Componente1.D5_PWM, S1.Pin_1, S1.Pin_2
  N11: Componente1.D6_PWM, LED6.cathode
  N12: Componente1.D7, LED5.cathode
  N13: Componente1.5V, R1.leg1, S1.Pin_3, S1.Pin_4, S2.Pin_3, S2.Pin_4
  N14: M1.pin_2, M2.pin_2

notes:
  Bomba de Água
  Motor Principal
  Nivel de Agua
  Modo de Operacao
  Seleciona o Nivel
  Seleciona o Modo
  Sensor de Nivel
